# Fritzing sketch elepi (saved by Fritzing 0.9.3b)
breadboards: 1

parts:
  S1 = Pushbutton [package="[THT]"]
  R2 = Resistor [tolerance=±5% resistance=10k package=THT]
  S2 = Pushbutton [package="[THT]"]
  S3 = Pushbutton [package="[THT]"]
  S4 = Pushbutton [package="[THT]"]
  S5 = Pushbutton [package="[THT]"]
  S6 = Pushbutton [package="[THT]"]
  S7 = Pushbutton [package="[THT]"]
  S8 = Pushbutton [package="[THT]"]
  R3 = Resistor [tolerance=±5% resistance=10k package=THT]
  R4 = Resistor [tolerance=±5% resistance=10k package=THT]
  R5 = Resistor [tolerance=±5% resistance=10k package=THT]
  R6 = Resistor [tolerance=±5% resistance=10k package=THT]
  R7 = Resistor [tolerance=±5% resistance=10k package=THT]
  R8 = Resistor [tolerance=±5% resistance=10k package=THT]
  R9 = Resistor [tolerance=±5% resistance=10k package=THT]
  R10 = Resistor [tolerance=±5% resistance=1k package=THT]
  J1 = Piezo Speaker
  Componente1 = Arduino Uno (Rev3) - ICSP

nets:
  N1: S1.Pin_1, S1.Pin_2, R2.Pin_0, Componente1.D2
  N2: S1.Pin_3, S1.Pin_4, S2.Pin_3, S2.Pin_4, S3.Pin_3, S3.Pin_4, S4.Pin_3, S4.Pin_4, S5.Pin_3, S5.Pin_4, S6.Pin_3, S6.Pin_4, S7.Pin_3, S7.Pin_4, S8.Pin_3, S8.Pin_4, Componente1.5V
  N3: R2.Pin_1, R3.Pin_1, R4.Pin_1, R5.Pin_1, R6.Pin_1, R7.Pin_1, R8.Pin_1, R9.Pin_1, J1.pin1, Componente1.GND
  N4: S2.Pin_1, S2.Pin_2, R9.Pin_0, Componente1.D9_PWM
  N5: S3.Pin_1, S3.Pin_2, R3.Pin_0, Componente1.D3_PWM
  N6: S4.Pin_1, S4.Pin_2, R4.Pin_0, Componente1.D4
  N7: S5.Pin_1, S5.Pin_2, R5.Pin_0, Componente1.D5_PWM
  N8: S6.Pin_1, S6.Pin_2, R8.Pin_0, Componente1.D8
  N9: S7.Pin_1, S7.Pin_2, R6.Pin_0, Componente1.D6_PWM
  N10: S8.Pin_1, S8.Pin_2, R7.Pin_0, Componente1.D7
  N11: R10.Pin_0, Componente1.D11_PWM/MOSI
  N12: R10.Pin_1, J1.pin2
