# Fritzing sketch elepi (saved by Fritzing 0.9.3b)
breadboards: 1

parts:
  S1 = Pushbutton [package="[THT]"]
  R2 = Resistor [tolerance=±5% resistance=10k package=THT]
  S2 = Pushbutton [package="[THT]"]
  S3 = Pushbutton [package="[THT]"]
  S4 = Pushbutton [package="[THT]"]
  S5 = Pushbutton [package="[THT]"]
  S6 = Pushbutton [package="[THT]"]
  S7 = Pushbutton [package="[THT]"]
  S8 = Pushbutton [package="[THT]"]
  R3 = Resistor [tolerance=±5% resistance=10k package=THT]
  R4 = Resistor [tolerance=±5% resistance=10k package=THT]
  R5 = Resistor [tolerance=±5% resistance=10k package=THT]
  R6 = Resistor [tolerance=±5% resistance=10k package=THT]
  R7 = Resistor [tolerance=±5% resistance=10k package=THT]
  R8 = Resistor [tolerance=±5% resistance=10k package=THT]
  R9 = Resistor [tolerance=±5% resistance=10k package=THT]
  R10 = Resistor [tolerance=±5% resistance=1k package=THT]
  J1 = Piezo Speaker
  Componente1 = Arduino Uno (Rev3) - ICSP

nets:
  N1: S1.Pin_1, S1.Pin_2, R2.Pin_0, Componente1.D2
  N2: S1.Pin_3, S1.Pin_4, S2.Pin_3, S2.Pin_4, S3.Pin_3, S3.Pin_4, S4.Pin_3, S4.Pin_4, S5.Pin_3, S5.Pin_4, S6.Pin_3, S6.Pin_4, S7.Pin_3, S7.Pin_4, S8.Pin_3, S8.Pin_4, Componente1.5V
  N3: R2.Pin_1, R3.Pin_1, R4.Pin_1, R5.Pin_1, R6.Pin_1, R7.Pin_1, R8.Pin_1, R9.Pin_1, J1.pin1, Componente1.GND
  N4: S2.Pin_1, S2.Pin_2, R9.Pin_0, Componente1.D9_PWM
  N5: S3.Pin_1, S3.Pin_2, R3.Pin_0, Componente1.D3_PWM
  N6: S4.Pin_1, S4.Pin_2, R4.Pin_0, Componente1.D4
  N7: S5.Pin_1, S5.Pin_2, R5.Pin_0, Componente1.D5_PWM
  N8: S6.Pin_1, S6.Pin_2, R8.Pin_0, Componente1.D8
  N9: S7.Pin_1, S7.Pin_2, R6.Pin_0, Componente1.D6_PWM
  N10: S8.Pin_1, S8.Pin_2, R7.Pin_0, Componente1.D7
  N11: R10.Pin_0, Componente1.D11_PWM/MOSI
  N12: R10.Pin_1, J1.pin2

// code stored in the sketch: elepi.ino
/**
 * Elepi - ELEctronic PIano
 * Copyright 2017-2019 Vitor Guia
 *
 * This program is free software: you can redistribute it and/or modify
 * it under the terms of the GNU General Public License as published by
 * the Free Software Foundation, either version 3 of the License, or
 * (at your option) any later version.
 *
 * This program is distributed in the hope that it will be useful,
 * but WITHOUT ANY WARRANTY; without even the implied warranty of
 * MERCHANTABILITY or FITNESS FOR A PARTICULAR PURPOSE.  See the
 * GNU General Public License for more details.
 *
 * You should have received a copy of the GNU General Public License
 * along with this program.  If not, see <https://www.gnu.org/licenses/>.
 *
 * Arduino version 2.0
 *
 * @author    Vitor Guia <contato@vitor.guia.nom.br>
 * @copyright 2019 Vitor Guia
 * @license   http://www.gnu.org/licenses GPL-3.0-or-later
 * @see       https://gitlab.com/vitoranguia/elepi Repository of Elepi
 */

const byte soundOut = 11;
int sleepNote = 1000;

/** Musical notes */
int DO = 262;  // or 261
int RE = 294;
int MI = 329;
int FA = 349;
int SOL = 392;
int LA = 440;
int SI = 494;
int DO2 = 523;

int notes[8] = {DO, RE, MI, FA, SOL, LA, SI, DO2};

void setup() {
    for (int i = 2; i < 10; i++) {
        pinMode(i, INPUT);
    }
}

void loop() {
    for (int i = 2; i < 10; i++) {
        if (digitalRead(i)) {
            tone(soundOut, notes[i-2], sleepNote);
        }
    }
}
